# Fritzing sketch arduino_spp_sensor_wiring (saved by Fritzing 0.9.0b)
breadboards: 2

parts:
  Part1 = Arduino Mega ADK (Rev3)
  LED1 = LED - 5mm [color="Red (633nm)" package="5 mm [THT]"]
  LED2 = smd LED [color="Yellow (592nm)" package="0603 [SMD]"]
  R3 = Resistor [tolerance=±5% resistance=1k package=THT]
  R4 = Resistor [tolerance=±5% resistance=1k package=THT]
  R1 = Rotary Potentiometer (Large) [maximum_resistance=100kΩ package=THT]
  LED3 = Red LED - 5mm [package="5 mm [THT]"]  # not connected

nets:
  N1: Part1.A2, R1.wiper
  N2: Part1.5V, R1.leg1
  N3: Part1.GND, R1.leg2
  N4: Part1.D2_PWM, R3.Pin_0
  N5: Part1.D3_PWM, R4.Pin_0
  N6: LED1.cathode, LED2.cathode
  N7: LED1.anode, R3.Pin_1
  N8: LED2.anode, R4.Pin_1

custom parts:
  Red LED - 5mm: A generic red LED (~1.8V)
